# Fritzing sketch 03-test-ds1820 (saved by Fritzing 0.8.5b)
breadboards: 1

parts:
  U3 = mystery part, 3 pins [chip_label=DS1820 spacing=300mil]
  Bauteil1 = Arduino Nano (Rev3.0)
  R1 = Resistor [tolerance=±10% resistance=4.7k package=THT]

nets:
  N1: U3.pin1, Bauteil1.GND
  N2: U3.pin2, Bauteil1.5V, R1.Pin_1
  N3: U3.pin3, Bauteil1.D3, R1.Pin_0
