# Fritzing sketch 05-test-esp288 (saved by Fritzing 0.8.5b)
breadboards: 1

parts:
  Bauteil1 = Arduino Nano (Rev3.0) (ICSP)
  U4 = ESP8266 WiFi Module [part_number=ESP8266]

nets:
  N1: Bauteil1.D1/TX, U4.TXD
  N2: Bauteil1.D0/RX, U4.RXD
  GND: Bauteil1.GND, U4.GND
  3V3: Bauteil1.3V3, U4.VCC, U4.CH_PD

custom parts:
  ESP8266 WiFi Module: Generic WiFi Module based on the ESP8266 with onboard PCB antenna and UART communications
