# Fritzing sketch 06-station-pcb (saved by Fritzing 0.8.5b)
circuit board: 7.53444cm x 2.08657cm

parts:
  DHT1 = DHT11 Humitidy and Temperature Sensor
  Arduino_Nano = Arduino Nano (Rev3.0)
  DS18B20 = mystery part, 3 pins [chip_label=DS1820 spacing=300mil]
  ESP8266 = ESP8266 WiFi Module [part_number=ESP8266]
  R1 = Resistor [tolerance=±5% resistance=4.7k package=THT]

nets:
  VDD: DHT1.VDD, Arduino_Nano.5V, DS18B20.pin3, R1.Pin_0
  N1: DHT1.DATA, Arduino_Nano.A0
  GND: DHT1.GND, Arduino_Nano.GND, DS18B20.pin1, ESP8266.GND
  N2: Arduino_Nano.D1/TX, ESP8266.RXD
  N3: Arduino_Nano.D0/RX, ESP8266.TXD
  N4: Arduino_Nano.D3, DS18B20.pin2, R1.Pin_1
  3V3: Arduino_Nano.3V3, ESP8266.VCC, ESP8266.CH_PD

notes:
  GND
  06-station-pcb.fzz
  18.10.2015
  https://github.com/schmiddim/arduino-weather-station

custom parts:
  DHT11 Humitidy and Temperature Sensor: DHT11 Humidity and Temperature Sensor
  ESP8266 WiFi Module: Generic WiFi Module based on the ESP8266 with onboard PCB antenna and UART communications
