# Fritzing sketch weather_station_nano_v3 (saved by Fritzing 0.8.5b)
circuit board: 7.53444cm x 2.08657cm

parts:
  DHT1 = DHT11 Humitidy and Temperature Sensor
  Bauteil1 = Arduino Nano (Rev3.0)
  U2 = mystery part, 3 pins [chip_label=DS1820 spacing=300mil]
  U3 = ESP8266 WiFi Module [part_number=ESP8266]
  R1 = Resistor [tolerance=±5% resistance=4.7k package=THT]

nets (from the schematic view):
  VDD: DHT1.VDD, Bauteil1.5V
  N1: DHT1.DATA, Bauteil1.A0
  GND: DHT1.GND, Bauteil1.GND, U2.pin1, U3.GND
  N2: Bauteil1.D1/TX, U3.RXD
  N3: Bauteil1.D0/RX, U3.TXD
  N4: Bauteil1.D3, U2.pin2, R1.Pin_1
  3V3: Bauteil1.3V3, U3.VCC, U3.CH_PD
  N5: U2.pin3, R1.Pin_0

custom parts:
  DHT11 Humitidy and Temperature Sensor: DHT11 Humidity and Temperature Sensor
  ESP8266 WiFi Module: Generic WiFi Module based on the ESP8266 with onboard PCB antenna and UART communications
